# Fritzing sketch v1 (saved by Fritzing 0.9.3b)
circuit board: 4.32781cm x 5.03815cm
breadboards: 1

parts:
  MAX_1 = MAX 7219 [package="DIP (Dual Inline) [THT]"]
  R1 = Resistor [tolerance=±5% resistance=220 package=THT]
  J1 = female pin header, 2 pins [form="♀ (female)"]
  J4 = female pin header, 8 pins [form="♀ (female)"]
  J5 = female pin header, 8 pins [form="♀ (female)"]
  J2 = female pin header, 4 pins [form="♀ (female)"]
  C1 = Electrolytic Capacitor [capacitance=1µF package="100 mil [THT, electrolytic]"]
  J6 = female pin header, 4 pins [form="♀ (female)"]
  C2 = Tantalum Capacitor [capacitance=1μF package="100 mil [THT, tantalum]"]

nets:
  N1: MAX_1.DIN, J1.pin1
  N2: MAX_1.DIG_0, J4.pin1
  N3: MAX_1.DIG_4, J4.pin2
  GND: MAX_1.GND, J2.pin2, C1.-, J6.pin2, C2.-
  N4: MAX_1.DIG_6, J4.pin3
  N5: MAX_1.DIG_2, J4.pin4
  N6: MAX_1.DIG_3, J4.pin5
  N7: MAX_1.DIG_7, J4.pin6
  N8: MAX_1.DIG_5, J4.pin7
  N9: MAX_1.DIG_1, J4.pin8
  N10: MAX_1.LOAD_(CS), J2.pin1, J6.pin1
  N11: MAX_1.CLK, J2.pin4, J6.pin4
  N12: MAX_1.SEG_A, J5.pin8
  N13: MAX_1.SEG_F, J5.pin7
  N14: MAX_1.SEG_B, J5.pin6
  N15: MAX_1.SEG_G, J5.pin5
  N16: MAX_1.ISET, R1.Pin_0
  5V: MAX_1.V+, R1.Pin_1, J2.pin3, C1.+, J6.pin3, C2.+
  N17: MAX_1.SEG_C, J5.pin4
  N18: MAX_1.SEG_E, J5.pin3
  N19: MAX_1.SEG_DP, J5.pin2
  N20: MAX_1.SEG_D, J5.pin1
  N21: MAX_1.DOUT, J1.pin2

custom parts:
  MAX 7219: A led matrix driver on a 300 mil dual inline package (DIP) footprint.
